// Digital circuit TGI-07-B.dig as structural Verilog
module TGI_07_B (
  input  S_0,
  input  R_0,
  input  S_1,
  input  R_1,
  input  Clock,
  input  S_2,
  input  R_2,
  input  Clock_2,
  input  S_3,
  input  R_3,
  input  Clock_3,
  output Q_0,
  output Q_0_2,
  output Q_1,
  output Q_1_2,
  output Q_2,
  output Q_2_2,
  output Q_3,
  output Q_3_2
);

  wire and_1_out, and_2_out, and_3_out, and_4_out, and_5_out, and_6_out, and_7_out, and_8_out, and_9_out,
       and_10_out, and_11_out, and_12_out, nand_1_out, nand_2_out, nand_3_out, nand_4_out;

  and and_1 (and_1_out, Q_3_2, S_3);
  and and_2 (and_2_out, R_3, Q_3);
  and and_3 (and_3_out, S_2, ~Clock_2);  // And
  and and_4 (and_4_out, ~Clock_2, R_2);  // And
  and and_5 (and_5_out, and_1_out, ~Clock_3);  // And
  and and_6 (and_6_out, ~Clock_3, and_2_out);  // And
  and and_7 (and_7_out, S_1, Clock);
  and and_8 (and_8_out, Clock, R_1);
  nand nand_1 (nand_1_out, ~and_3_out, nand_2_out);  // NAnd
  nand nand_2 (nand_2_out, nand_1_out, ~and_4_out);  // NAnd
  nand nand_3 (nand_3_out, ~and_5_out, nand_4_out);  // NAnd
  nand nand_4 (nand_4_out, nand_3_out, ~and_6_out);  // NAnd
  nand nand_5 (Q_0, ~S_0, Q_0_2);  // NAnd
  nand nand_6 (Q_0_2, Q_0, ~R_0);  // NAnd
  nand nand_7 (Q_1, ~and_7_out, Q_1_2);  // NAnd
  nand nand_8 (Q_1_2, Q_1, ~and_8_out);  // NAnd
  and and_9 (and_9_out, Clock_2, nand_1_out);
  and and_10 (and_10_out, nand_2_out, Clock_2);
  and and_11 (and_11_out, Clock_3, nand_3_out);
  and and_12 (and_12_out, nand_4_out, Clock_3);
  nand nand_9 (Q_2, ~and_9_out, Q_2_2);  // NAnd
  nand nand_10 (Q_2_2, Q_2, ~and_10_out);  // NAnd
  nand nand_11 (Q_3, ~and_11_out, Q_3_2);  // NAnd
  nand nand_12 (Q_3_2, Q_3, ~and_12_out);  // NAnd

  // Notes on the sheet:
  //   Aufgabe 3
  //   Aufgabe 0
  //   Aufgabe 1
  //   Aufgabe 2
endmodule
